# Fritzing sketch Umbrella_Dryer_Wiring_Diagram (saved by Fritzing 0.9.3b)
breadboards: 1

parts:
  Part1 = Arduino Uno (Rev3) - ICSP
  RY1 = SSR-40VA
  RY2 = SSR-40VA
  A1 = DHT22 module
  S1 = Momentary Switch [package=ksa_sealed_tac_switch]
  S2 = Momentary Switch [package=ksa_sealed_tac_switch]
  S3 = Momentary Switch [package=ksa_sealed_tac_switch]
  S4 = Momentary Switch [package=ksa_sealed_tac_switch]
  LCD2004-I2C1 = LCD2004-I2C
  F1 = Fan - Ventilador [package=THT]
  A2 = Dryer heater
  R1 = Resistor [tolerance=±5% resistance=220 package="0402 [SMD]"]
  R2 = Resistor [tolerance=±5% resistance=220 package="0402 [SMD]"]
  R3 = Resistor [tolerance=±5% resistance=220 package="0402 [SMD]"]
  R4 = Resistor [tolerance=±5% resistance=220 package="0402 [SMD]"]
  LED1 = RGB LED - (4 legs) [package="5 mm [THT]"]
  M1 = RioRand LM2596
  HLK-PM1 = HLK-PM12 [part_number=HLK-PM12]
  D1 = Rectifier Diode [part_number=1N4001 package="Melf DO-213 AB [SMD]"]
  R5 = Resistor [tolerance=±5% resistance=220 package="0402 [SMD]"]
  R6 = Resistor [tolerance=±5% resistance=220 package="0402 [SMD]"]
  R7 = Resistor [tolerance=±5% resistance=220 package="0402 [SMD]"]
  C1 = Electrolytic Capacitor [capacitance=100µF package="200 mil [THT, electrolytic]"]

nets:
  N1: Part1.D8, RY2.Pin_3
  N2: Part1.D9_PWM, RY1.Pin_3
  N3: Part1.D10_PWM/SS, A1.Out
  N4: Part1.D11_PWM/MOSI, R7.Pin_1
  GND: Part1.GND, RY1.Pin_4, RY2.Pin_4, A1.-, S1.3, S2.3, S3.3, S4.3, LCD2004-I2C1.GND, M1.Pin_4, C1.-
  N5: Part1.A4/SDA, LCD2004-I2C1.SCL
  N6: Part1.A5/SCL, LCD2004-I2C1.SDA
  N7: Part1.D2, R5.Pin_1
  N8: Part1.D3_PWM, R6.Pin_1
  N9: Part1.D4, S3.2, R4.Pin_0, R4.Pin_1
  N10: Part1.D5_PWM, S1.2, R3.Pin_0, R3.Pin_1
  N11: Part1.D6_PWM, S2.2, R2.Pin_0, R2.Pin_1
  N12: Part1.D7, S4.2, R1.Pin_0, R1.Pin_1
  5V: Part1.5V, A1.+, LCD2004-I2C1.VCC
  N13: Part1.VIN, D1.cathode, C1.+
  N14: RY1.Pin_1, F1.5V
  N15: RY1.Pin_2, RY2.Pin_2, HLK-PM1.AC_2
  N16: RY2.Pin_1, A2.Pin_2
  N17: F1.GND, A2.Pin_1, HLK-PM1.AC_1
  N18: LED1.red_cathode, R5.Pin_0
  N19: LED1.green_cathode, R6.Pin_0
  N20: LED1.blue_cathode, R7.Pin_0
  N21: M1.Pin_1, HLK-PM1.+Vo
  N22: M1.Pin_2, HLK-PM1.-Vo
  N23: M1.Pin_3, D1.anode

custom parts:
  SSR-40VA: SSR-40VA solid state relay.
  DHT22 module: DHT22 module. Pins VCC Data GND.
  LCD2004-I2C: A standard character display with 4x20 characters. Comes in many colors with LCM2004 IIC attached.
  Fan - Ventilador: Ventilador de 2 pines, se encuentra comunmente en computadoras de escritorio
  Dryer heater: Dryer heater.
